// Digital circuit dac.dig as structural Verilog
module dac (
  input  [2:0] D_r,
  input  [2:0] D_g,
  input  [1:0] D_b,
  output R,
  output G,
  output B
);

  and and_1 (R, D_r[0], D_r[1], D_r[2]);
  and and_2 (G, D_g[0], D_g[1], D_g[2]);
  and and_3 (B, D_b[0], D_b[1]);
endmodule
