// Digital circuit tile_logic.dig as structural Verilog
module tile_logic (
  input  [9:0] SX,
  input  [9:0] SY,
  input  nMREQ,
  input  nVRAM_E,
  input  VBLANK,
  input  [9:0] COL,
  input  [9:0] ROW,
  input  A14,
  input  HBLANK,
  output [7:0] PIX
);

  wire CE_IR, CE_IR_CPU_BUS, CE_TR, CE_TR_CPU_BUS, nand_1_out, nand_2_out, nor_1_out, nor_2_out, nor_3_out,
       nor_4_out, not_1_out, or_1_out, or_2_out, or_3_out;
  wire [7:0] Index_ROM_d;
  wire [9:0] add_1_s, add_2_s;

  or or_1 (or_1_out, nVRAM_E, nMREQ);
  nor nor_1 (nor_1_out, A14, A14);
  or or_2 (or_2_out, or_1_out, A14);
  or or_3 (or_3_out, or_1_out, nor_1_out);
  not not_1 (not_1_out, VBLANK);
  nor nor_2 (nor_2_out, not_1_out, or_2_out);
  nor nor_3 (nor_3_out, not_1_out, or_3_out);
  nand nand_1 (nand_1_out, or_2_out, VBLANK);
  nand nand_2 (nand_2_out, or_3_out, VBLANK);
  nand nand_3 (CE_TR_CPU_BUS, nor_2_out, nor_2_out);
  nand nand_4 (CE_IR_CPU_BUS, nor_3_out, nor_3_out);
  nand nand_5 (CE_TR, nand_1_out, nand_1_out);
  nand nand_6 (CE_IR, nand_2_out, nand_2_out);
  Add #(.Bits(10)) add_1 (.a(SX), .b(COL), .c_i(1'b0), .s(add_1_s));  // open: c_o
  Add #(.Bits(10)) add_2 (.a(SY), .b(ROW), .c_i(1'b0), .s(add_2_s));  // open: c_o
  ROM #(.AddrBits(14), .Bits(8)) Index_ROM (.A({add_2_s[9:3], add_1_s[9:3]}), .sel(1'b1), .D(Index_ROM_d));
  nor nor_4 (nor_4_out, HBLANK, VBLANK);
  ROM #(.AddrBits(14), .Bits(8)) Tile_ROM (.A({Index_ROM_d, add_2_s[2:0], add_1_s[2:0]}), .sel(nor_4_out), .D(PIX));

  // Notes on the sheet:
  //   contents of Index_ROM (hex, n*v repeats v):
  //   61,49,13,26,35,51,7,90,70,25,40,92,9,91,0,65,29,35,2,13,90,81
  //   ,39,51,64,74,52,44,11,44,37,16,93,94,43,73,89,50,7,4,20,47,96
  //   ,73,83,96,82,56,75,84,69,9,10,53,61,74,27,57,18,83,1,99,99,39
  //   ,37,42,12,27,37,19,31,1,11,27,18,38,67,0,94,42,28,7,52,38,60,57
  //   ,56,32,58,18,15,4,61,14,43,99,1,99,26,82,62,1,27,17,72,45,55,39
  //   ,89,49,25,61,57,21,44,17,22,0,49,81,63,8,85,24,67,72,23,12,71
  //   ,93,94,33,38,65,51,10,54,50,93,43,0,63,48,1,28,92,62,51,37,56
  //   ,76,0,64,5,24,31,77,92,43,48,29,81,25,68,46,20,22,44,15,16,31
  //   ,15,79,80,60,7,72,22,2,9,78,78,53,87,83,22,62,4,14,50,52,87,31
  //   ,22,55,22,86,22,10,1,38,42,60,61,22,20,12,38,87,15,48,9,37,45
  //   ,96,21,67,59,25,25,9,22,13,84,88,12,50,18,34,61,64,16,3,24,77
  //   ,69,89,90,7,20,5,99,29,42,45,26,7,12,29,77,38,38,43,95,66,75,7
  //   ,61,93,86,22,1,2,69,26,80,38,59,14,89,79,19,89,8,5,78,78,57,34
  //   ,7,78,16,89,21,11,0,40,63,61,33,49,27,35,51,96,5,75,78,8,89,11
  //   ,31,52,0,39,2,22,62,3,57,69,81,73,3,46,85,3,86,48,64,63,41,91
  //   ,42,36,31,47,56,9,99,45,20,30,42,65,14,44,87,76,47,44,89,72,62
  //   ,92,18,47,95,4,39,59,11,24,50,54,4,25,45,60,34,45,50,99,19,92
  //   ,8,33,80,39,53,71,28,43,43,90,35,5,81,75,53,64,34,64,88,29,18
  //   ,92,54,64,53,33,53,47,76,72,39,28,6,63,67,3,78,95,46,65,85,26
  //   ,70,10,1,23,74,79,31,6,52,50,99,51,58,96,28,11,43,48,83,26,76
  //   ,33,33,43,37,11,39,27,20,68,53,90,79,98,57,53,22,88,4,74,82,3
  //   ,69,40,43,97,51,30,45,79,0,65,56,33,9,93,88,92,21,8,4,18,42,27
  //   ,17,43,25,39,31,29,57,58,32,27,98,19,68,94,49,58,17,93,23,73,70
  //   ,76,11,2,12,76,10,17,94,96,44,55,39,13,38,14,42,40,72,18,11,15
  //   ,37,79,53,30,81,70,23,49,87,37,25,98,39,82,18,49,43,13,89,31,12
  //   ,28,45,51,87,87,35,3,6,46,18,43,25,71,18,51,85,85,0,73,23,69,15
  //   ,62,51,34,56,94,91,45,26,3,18,15,98,49,2,33,52,8,23,71,96,49,86
  //   ,58,44,72,43,44,89,10,13,4,73,9,82,73,47,73,62,17,21,24,32,63
  //   ,73,35,41,26,87,64,41,27,57,27,85,1,43,29,45,32,39,3,81,56,56
  //   ,63,29,3,81,36,21,2,60,53,9,34,32,50,4,20,15,45,47,72,72,33,18
  //   ,16,6,7,92,89,10,73,90,10,81,63,14,62,99,35,8,60,32,17,38,65,68
  //   ,42,29,27,87,76,99,3,53,17,19,3,25,56,37,79,29,27,90,54,90,48
  //   ,16,34,27,68,94,59,86,32,68,98,18,97,25,5,18,68,8,71,30,72,19
  //   ,55,28,56,78,1,83,12,56,17,60,16,51,87,85,89,91,15,65,59,13,83
  //   ,1,82,88,19,50,41,90,80,13,9,79,41,9,2,86,92,14,42,54,19,3,5,50
  //   ,32,39,41,47,4,45,4,88,46,86,20,65,80,61,55,5,18,9,84,3,18,30
  //   ,90,55,45,76,9,8,79,58,58,11,97,44,2,46,89,6,34,35,36,98,0,17
  //   ,4,99,22,22,52,50,26,15,81,16,14,70,92,23,22,16,25,80,71,67,24
  //   ,74,13,57,24,91,92,5,89,36,22,93,80,88,16,32,82,42,91,7,2,5,77
  //   ,38,72,99,54,98,24,26,9,92,44,22,50,12,13,86,17,46,23,39,84,47
  //   ,71,44,23,54,30,15,5,32,20,83,70,37,26,69,35,50,39,44,87,83,10
  //   ,37,95,67,67,13,13,34,96,41,81,12,85,5,10,15,20,15,47,84,42,62
  //   ,21,69,31,0,63,14,88,50,97,42,31,36,9,43,93,67,77,34,8,59,46,94
  //   ,8,0,53,28,15,45,56,58,7,22,71,82,66,34,96,55,29,37,41,4,17,51
  //   ,47,11,18,69,45,70,28,35,8,36,35,62,8,50,7,8,52,58,30,23,40,41
  //   ,2,80,40,75,61,81,23,78,32,15,89,94,84,78,9,56,13,17,36,48,79
  //   ,44,43,86,96,95,44,71,19,28,12,65,52,52,40,13,33,63,36,10,78,25
  //   ,48,6,48,57,62,61,75,98,54,54,86,97,85,83,92,73,54,55,46,10,20
  //   ,42,6,4,0,39,12,36,93,90,5,86,97,53,43,3,15,62,2,13,61,88,10,90
  //   ,15,46,7,13,2,53,23,66,96,29,15,96,13,27,32,50,17,37,36,58,35
  //   ,24,62,50,30,8,7,35,96,17,25,56,63,33,69,9,30,37,20,26,10,35,66
  //   ,67,62,42,18,23,24,98,82,59,66,88,53,41,96,60,76,36,21,2,92,84
  //   ,79,6,38,9,43,58,80,53,93,46,65,55,33,27,78,1,25,4,60,36,92,57
  //   ,77,32,17,53,69,38,99,61,66,22,67,4,32,54,6,12,52,99,2,17,54,79
  //   ,44,77,80,13,25,40,49,18,41,70,50,2,68,63,40,11,25,51,34,36,99
  //   ,10,91,6,22,43,5,68,4,4,48,48,25,72,5,50,57,99,12,98,13,7,1,81
  //   ,70,85,37,39,36,71,20,80,81,11,86,47,98,35,59,46,83,51,38,8,24
  //   ,43,3,81,42,15,23,0,66,24,81,37,10,18,20,90,33,40,14,58,95,0,5
  //   ,37,80,9,83,63,60,21,16,84,9,19,9,51,78,33,51,45,1,77,26,11,39
  //   ,90,46,17,31,60,75,70,5,25,8,85,34,91,92,94,57,8,23,66,71,32,61
  //   ,94,9,57,83,11,34,53,22,17,43,12,34,18,17,10,89,22,35,41,51,13
  //   ,32,43,7,33,96,30,99,11,7,61,5,16,18,88,27,96,41,50,57,29,6,92
  //   ,47,23,46,80,45,25,21,40,38,98,84,45,31,24,20,75,35,27,36,41,43
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  //   contents of Tile_ROM (hex, n*v repeats v):
  //   61,49,13,26,35,51,7,90,70,25,40,92,9,91,0,65,29,35,2,13,90,81
  //   ,39,51,64,74,52,44,11,44,37,16,93,94,43,73,89,50,7,4,20,47,96
  //   ,73,83,96,82,56,75,84,69,9,10,53,61,74,27,57,18,83,1,99,99,39
  //   ,37,42,12,27,37,19,31,1,11,27,18,38,67,0,94,42,28,7,52,38,60,57
  //   ,56,32,58,18,15,4,61,14,43,99,1,99,26,82,62,1,27,17,72,45,55,39
  //   ,89,49,25,61,57,21,44,17,22,0,49,81,63,8,85,24,67,72,23,12,71
  //   ,93,94,33,38,65,51,10,54,50,93,43,0,63,48,1,28,92,62,51,37,56
  //   ,76,0,64,5,24,31,77,92,43,48,29,81,25,68,46,20,22,44,15,16,31
  //   ,15,79,80,60,7,72,22,2,9,78,78,53,87,83,22,62,4,14,50,52,87,31
  //   ,22,55,22,86,22,10,1,38,42,60,61,22,20,12,38,87,15,48,9,37,45
  //   ,96,21,67,59,25,25,9,22,13,84,88,12,50,18,34,61,64,16,3,24,77
  //   ,69,89,90,7,20,5,99,29,42,45,26,7,12,29,77,38,38,43,95,66,75,7
  //   ,61,93,86,22,1,2,69,26,80,38,59,14,89,79,19,89,8,5,78,78,57,34
  //   ,7,78,16,89,21,11,0,40,63,61,33,49,27,35,51,96,5,75,78,8,89,11
  //   ,31,52,0,39,2,22,62,3,57,69,81,73,3,46,85,3,86,48,64,63,41,91
  //   ,42,36,31,47,56,9,99,45,20,30,42,65,14,44,87,76,47,44,89,72,62
  //   ,92,18,47,95,4,39,59,11,24,50,54,4,25,45,60,34,45,50,99,19,92
  //   ,8,33,80,39,53,71,28,43,43,90,35,5,81,75,53,64,34,64,88,29,18
  //   ,92,54,64,53,33,53,47,76,72,39,28,6,63,67,3,78,95,46,65,85,26
  //   ,70,10,1,23,74,79,31,6,52,50,99,51,58,96,28,11,43,48,83,26,76
  //   ,33,33,43,37,11,39,27,20,68,53,90,79,98,57,53,22,88,4,74,82,3
  //   ,69,40,43,97,51,30,45,79,0,65,56,33,9,93,88,92,21,8,4,18,42,27
  //   ,17,43,25,39,31,29,57,58,32,27,98,19,68,94,49,58,17,93,23,73,70
  //   ,76,11,2,12,76,10,17,94,96,44,55,39,13,38,14,42,40,72,18,11,15
  //   ,37,79,53,30,81,70,23,49,87,37,25,98,39,82,18,49,43,13,89,31,12
  //   ,28,45,51,87,87,35,3,6,46,18,43,25,71,18,51,85,85,0,73,23,69,15
  //   ,62,51,34,56,94,91,45,26,3,18,15,98,49,2,33,52,8,23,71,96,49,86
  //   ,58,44,72,43,44,89,10,13,4,73,9,82,73,47,73,62,17,21,24,32,63
  //   ,73,35,41,26,87,64,41,27,57,27,85,1,43,29,45,32,39,3,81,56,56
  //   ,63,29,3,81,36,21,2,60,53,9,34,32,50,4,20,15,45,47,72,72,33,18
  //   ,16,6,7,92,89,10,73,90,10,81,63,14,62,99,35,8,60,32,17,38,65,68
  //   ,42,29,27,87,76,99,3,53,17,19,3,25,56,37,79,29,27,90,54,90,48
  //   ,16,34,27,68,94,59,86,32,68,98,18,97,25,5,18,68,8,71,30,72,19
  //   ,55,28,56,78,1,83,12,56,17,60,16,51,87,85,89,91,15,65,59,13,83
  //   ,1,82,88,19,50,41,90,80,13,9,79,41,9,2,86,92,14,42,54,19,3,5,50
  //   ,32,39,41,47,4,45,4,88,46,86,20,65,80,61,55,5,18,9,84,3,18,30
  //   ,90,55,45,76,9,8,79,58,58,11,97,44,2,46,89,6,34,35,36,98,0,17
  //   ,4,99,22,22,52,50,26,15,81,16,14,70,92,23,22,16,25,80,71,67,24
  //   ,74,13,57,24,91,92,5,89,36,22,93,80,88,16,32,82,42,91,7,2,5,77
  //   ,38,72,99,54,98,24,26,9,92,44,22,50,12,13,86,17,46,23,39,84,47
  //   ,71,44,23,54,30,15,5,32,20,83,70,37,26,69,35,50,39,44,87,83,10
  //   ,37,95,67,67,13,13,34,96,41,81,12,85,5,10,15,20,15,47,84,42,62
  //   ,21,69,31,0,63,14,88,50,97,42,31,36,9,43,93,67,77,34,8,59,46,94
  //   ,8,0,53,28,15,45,56,58,7,22,71,82,66,34,96,55,29,37,41,4,17,51
  //   ,47,11,18,69,45,70,28,35,8,36,35,62,8,50,7,8,52,58,30,23,40,41
  //   ,2,80,40,75,61,81,23,78,32,15,89,94,84,78,9,56,13,17,36,48,79
  //   ,44,43,86,96,95,44,71,19,28,12,65,52,52,40,13,33,63,36,10,78,25
  //   ,48,6,48,57,62,61,75,98,54,54,86,97,85,83,92,73,54,55,46,10,20
  //   ,42,6,4,0,39,12,36,93,90,5,86,97,53,43,3,15,62,2,13,61,88,10,90
  //   ,15,46,7,13,2,53,23,66,96,29,15,96,13,27,32,50,17,37,36,58,35
  //   ,24,62,50,30,8,7,35,96,17,25,56,63,33,69,9,30,37,20,26,10,35,66
  //   ,67,62,42,18,23,24,98,82,59,66,88,53,41,96,60,76,36,21,2,92,84
  //   ,79,6,38,9,43,58,80,53,93,46,65,55,33,27,78,1,25,4,60,36,92,57
  //   ,77,32,17,53,69,38,99,61,66,22,67,4,32,54,6,12,52,99,2,17,54,79
  //   ,44,77,80,13,25,40,49,18,41,70,50,2,68,63,40,11,25,51,34,36,99
  //   ,10,91,6,22,43,5,68,4,4,48,48,25,72,5,50,57,99,12,98,13,7,1,81
  //   ,70,85,37,39,36,71,20,80,81,11,86,47,98,35,59,46,83,51,38,8,24
  //   ,43,3,81,42,15,23,0,66,24,81,37,10,18,20,90,33,40,14,58,95,0,5
  //   ,37,80,9,83,63,60,21,16,84,9,19,9,51,78,33,51,45,1,77,26,11,39
  //   ,90,46,17,31,60,75,70,5,25,8,85,34,91,92,94,57,8,23,66,71,32,61
  //   ,94,9,57,83,11,34,53,22,17,43,12,34,18,17,10,89,22,35,41,51,13
  //   ,32,43,7,33,96,30,99,11,7,61,5,16,18,88,27,96,41,50,57,29,6,92
  //   ,47,23,46,80,45,25,21,40,38,98,84,45,31,24,20,75,35,27,36,41,43
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endmodule
