// Digital circuit 74ACT374.dig as structural Verilog
module _74ACT374 (
  input  D0,
  input  D1,
  input  D2,
  input  D3,
  input  D4,
  input  D5,
  input  D6,
  input  D7,
  input  Cp,
  input  nOE,
  output O0,
  output O1,
  output O2,
  output O3,
  output O4,
  output O5,
  output O6,
  output O7
);

  wire not_1_out;
  wire [7:0] register_1_q;

  Register #(.Bits(8)) register_1 (.D({D7, D6, D5, D4, D3, D2, D1, D0}), .C(Cp), .en(1'b1), .Q(register_1_q));
  not not_1 (not_1_out, nOE);
  assign {O7, O6, O5, O4, O3, O2, O1, O0} = not_1_out ? register_1_q : 8'bz;  // Driver driver_1
endmodule
