// Digital circuit tile_logic.dig as structural Verilog
module tile_logic (
  input  [9:0] COL,
  input  [9:0] ROW,
  input  HBLANK,
  input  VBLANK,
  input  PIX_CLK,
  input  [7:0] D,
  input  [21:0] A,
  input  MREQ,
  input  RD,
  input  WR,
  input  IOSELx,
  output [7:0] PIX,
  output VBI_CLR
);

  wire _74541_2_pin11, _74541_2_pin12, _74541_6_pin11, _74541_6_pin12, add_1_c_o, add_2_c_o, add_4_c_o,
       add_5_c_o, bussplitter_1_d0, bussplitter_1_d1, bussplitter_1_d2, bussplitter_1_d3, bussplitter_1_d4,
       bussplitter_1_d5, bussplitter_1_d6, bussplitter_1_d7, bussplitter_2_d0, bussplitter_2_d1,
       bussplitter_2_d2, bussplitter_2_d3, bussplitter_2_d4, bussplitter_2_d5, bussplitter_2_d6,
       bussplitter_2_d7, CE_IR, CE_IR_CPU_BUS, CE_TR, CE_TR_CPU_BUS, INDEX_RAM_PAGE, nand_1_out, nand_3_out,
       nand_4_out, nand_5_out, nor_2_out, nor_3_out, nor_4_out, nor_5_out, nor_6_out, nor_7_out, nor_8_out,
       NOT_RD, NOT_VBLANK, or_1_out, or_2_out, or_3_out, or_4_out, TILE_RAM_PAGE;
  wire [0:0] add_4_s_2;
  wire [1:0] _74541_5_pin8;
  wire [2:0] add_1_s, add_4_s;
  wire [3:2] add_3_s_2, add_6_s_2;
  wire [5:0] _74541_2_pin13, _74541_6_pin2, _74541_6_pin18, add_6_s;
  wire [6:0] add_3_s;
  wire [7:0] _74541_1_pin11, _74541_5_pin18, ramsingleportsel_2_d;
  wire [9:0] SX, SY;

  nor nor_1 (NOT_RD, RD, RD);
  nor nor_2 (nor_2_out, IOSELx, A[0]);
  nor nor_3 (nor_3_out, IOSELx, A[1]);
  nor nor_4 (nor_4_out, IOSELx, A[2]);
  _74574 _74574_1 (
    .pin1(1'b0), .pin2(D[0]), .pin3(D[1]), .pin4(D[2]), .pin5(D[3]), .pin6(D[4]), .pin7(D[5]), .pin8(D[6]),
    .pin9(D[7]), .pin10(1'b0), .pin11(nor_2_out), .pin12(SX[7]), .pin13(SX[6]), .pin14(SX[5]), .pin15(SX[4]),
    .pin16(SX[3]), .pin17(SX[2]), .pin18(SX[1]), .pin19(SX[0]), .pin20(1'b1));
  _74574 _74574_2 (
    .pin1(1'b0), .pin2(D[0]), .pin3(D[1]), .pin4(D[2]), .pin5(D[3]), .pin6(D[4]), .pin7(D[5]), .pin8(D[6]),
    .pin9(D[7]), .pin10(1'b0), .pin11(nor_3_out), .pin12(TILE_RAM_PAGE), .pin13(INDEX_RAM_PAGE),
    .pin14(VBI_CLR), .pin16(SY[9]), .pin17(SY[8]), .pin18(SX[9]), .pin19(SX[8]), .pin20(1'b1));  // open: pin15
  _74574 _74574_3 (
    .pin1(1'b0), .pin2(D[0]), .pin3(D[1]), .pin4(D[2]), .pin5(D[3]), .pin6(D[4]), .pin7(D[5]), .pin8(D[6]),
    .pin9(D[7]), .pin10(1'b0), .pin11(nor_4_out), .pin12(SY[7]), .pin13(SY[6]), .pin14(SY[5]), .pin15(SY[4]),
    .pin16(SY[3]), .pin17(SY[2]), .pin18(SY[1]), .pin19(SY[0]), .pin20(1'b1));
  nand nand_1 (nand_1_out, A[19], A[19]);
  nand nand_2 (NOT_VBLANK, VBLANK, VBLANK);
  nand nand_3 (nand_3_out, A[15], A[15], A[16], A[17], A[18], nand_1_out, A[20], A[21]);
  or or_1 (or_1_out, nand_3_out, MREQ);
  nor nor_5 (nor_5_out, A[14], A[14]);
  or or_2 (or_2_out, or_1_out, A[14]);
  or or_3 (or_3_out, or_1_out, nor_5_out);
  nor nor_6 (nor_6_out, NOT_VBLANK, or_2_out);
  nor nor_7 (nor_7_out, NOT_VBLANK, or_3_out);
  nand nand_4 (nand_4_out, or_2_out, VBLANK);
  nand nand_5 (nand_5_out, or_3_out, VBLANK);
  nand nand_6 (CE_TR_CPU_BUS, nor_6_out, nor_6_out);
  nand nand_7 (CE_IR_CPU_BUS, nor_7_out, nor_7_out);
  nand nand_8 (CE_TR, nand_4_out, nand_4_out);
  nand nand_9 (CE_IR, nand_5_out, nand_5_out);
  Add #(.Bits(4)) add_1 (.a(COL[3:0]), .b(SX[3:0]), .c_i(1'b0), .s({add_3_s[0], add_1_s}), .c_o(add_1_c_o));
  Add #(.Bits(4)) add_2 (.a(COL[7:4]), .b(SX[7:4]), .c_i(add_1_c_o), .s(add_3_s[4:1]), .c_o(add_2_c_o));
  Add #(.Bits(4)) add_3 (
    .a({2'b00, COL[9:8]}), .b({2'b00, SX[9:8]}), .c_i(add_2_c_o), .s({add_3_s_2, add_3_s[6:5]}));  // open: c_o
  Add #(.Bits(4)) add_4 (.a(ROW[3:0]), .b(SY[3:0]), .c_i(1'b0), .s({add_4_s_2[0], add_4_s}), .c_o(add_4_c_o));
  Add #(.Bits(4)) add_5 (.a(ROW[7:4]), .b(SY[7:4]), .c_i(add_4_c_o), .s(add_6_s[3:0]), .c_o(add_5_c_o));
  Add #(.Bits(4)) add_6 (
    .a({2'b00, ROW[9:8]}), .b({2'b00, SY[9:8]}), .c_i(add_5_c_o), .s({add_6_s_2, add_6_s[5:4]}));  // open: c_o
  _74541 _74541_1 (
    .pin1(VBLANK), .pin2(add_3_s[0]), .pin3(add_3_s[1]), .pin4(add_3_s[2]), .pin5(add_3_s[3]),
    .pin6(add_3_s[4]), .pin7(add_3_s[5]), .pin8(add_3_s[6]), .pin9(add_4_s_2[0]), .pin10(1'b0),
    .pin11(_74541_1_pin11[7]), .pin12(_74541_1_pin11[6]), .pin13(_74541_1_pin11[5]),
    .pin14(_74541_1_pin11[4]), .pin15(_74541_1_pin11[3]), .pin16(_74541_1_pin11[2]),
    .pin17(_74541_1_pin11[1]), .pin18(_74541_1_pin11[0]), .pin19(1'b0), .pin20(1'b1));
  _74541 _74541_2 (
    .pin1(VBLANK), .pin2(add_6_s[0]), .pin3(add_6_s[1]), .pin4(add_6_s[2]), .pin5(add_6_s[3]),
    .pin6(add_6_s[4]), .pin7(add_6_s[5]), .pin8(1'b1), .pin9(1'b0), .pin10(1'b0), .pin11(_74541_2_pin11),
    .pin12(_74541_2_pin12), .pin13(_74541_2_pin13[5]), .pin14(_74541_2_pin13[4]), .pin15(_74541_2_pin13[3]),
    .pin16(_74541_2_pin13[2]), .pin17(_74541_2_pin13[1]), .pin18(_74541_2_pin13[0]), .pin19(1'b0),
    .pin20(1'b1));
  _74541 _74541_3 (
    .pin1(NOT_VBLANK), .pin2(A[0]), .pin3(A[1]), .pin4(A[2]), .pin5(A[3]), .pin6(A[4]), .pin7(A[5]),
    .pin8(A[6]), .pin9(A[7]), .pin10(1'b0), .pin11(_74541_1_pin11[7]), .pin12(_74541_1_pin11[6]),
    .pin13(_74541_1_pin11[5]), .pin14(_74541_1_pin11[4]), .pin15(_74541_1_pin11[3]),
    .pin16(_74541_1_pin11[2]), .pin17(_74541_1_pin11[1]), .pin18(_74541_1_pin11[0]), .pin19(1'b0),
    .pin20(1'b1));
  _74541 _74541_4 (
    .pin1(NOT_VBLANK), .pin2(A[8]), .pin3(A[9]), .pin4(A[10]), .pin5(A[11]), .pin6(A[12]), .pin7(A[13]),
    .pin8(WR), .pin9(RD), .pin10(1'b0), .pin11(_74541_2_pin11), .pin12(_74541_2_pin12),
    .pin13(_74541_2_pin13[5]), .pin14(_74541_2_pin13[4]), .pin15(_74541_2_pin13[3]),
    .pin16(_74541_2_pin13[2]), .pin17(_74541_2_pin13[1]), .pin18(_74541_2_pin13[0]), .pin19(1'b0),
    .pin20(1'b1));
  _74541 _74541_5 (
    .pin1(VBLANK), .pin2(add_1_s[0]), .pin3(add_1_s[1]), .pin4(add_1_s[2]), .pin5(add_4_s[0]),
    .pin6(add_4_s[1]), .pin7(add_4_s[2]), .pin8(_74541_5_pin8[0]), .pin9(_74541_5_pin8[1]), .pin10(1'b0),
    .pin11(_74541_5_pin18[7]), .pin12(_74541_5_pin18[6]), .pin13(_74541_5_pin18[5]),
    .pin14(_74541_5_pin18[4]), .pin15(_74541_5_pin18[3]), .pin16(_74541_5_pin18[2]),
    .pin17(_74541_5_pin18[1]), .pin18(_74541_5_pin18[0]), .pin19(1'b0), .pin20(1'b1));
  _74541 _74541_6 (
    .pin1(VBLANK), .pin2(_74541_6_pin2[0]), .pin3(_74541_6_pin2[1]), .pin4(_74541_6_pin2[2]),
    .pin5(_74541_6_pin2[3]), .pin6(_74541_6_pin2[4]), .pin7(_74541_6_pin2[5]), .pin8(1'b1), .pin9(1'b0),
    .pin10(1'b0), .pin11(_74541_6_pin11), .pin12(_74541_6_pin12), .pin13(_74541_6_pin18[5]),
    .pin14(_74541_6_pin18[4]), .pin15(_74541_6_pin18[3]), .pin16(_74541_6_pin18[2]),
    .pin17(_74541_6_pin18[1]), .pin18(_74541_6_pin18[0]), .pin19(1'b0), .pin20(1'b1));
  _74541 _74541_7 (
    .pin1(NOT_VBLANK), .pin2(A[0]), .pin3(A[1]), .pin4(A[2]), .pin5(A[3]), .pin6(A[4]), .pin7(A[5]),
    .pin8(A[6]), .pin9(A[7]), .pin10(1'b0), .pin11(_74541_5_pin18[7]), .pin12(_74541_5_pin18[6]),
    .pin13(_74541_5_pin18[5]), .pin14(_74541_5_pin18[4]), .pin15(_74541_5_pin18[3]),
    .pin16(_74541_5_pin18[2]), .pin17(_74541_5_pin18[1]), .pin18(_74541_5_pin18[0]), .pin19(1'b0),
    .pin20(1'b1));
  _74541 _74541_8 (
    .pin1(NOT_VBLANK), .pin2(A[8]), .pin3(A[9]), .pin4(A[10]), .pin5(A[11]), .pin6(A[12]), .pin7(A[13]),
    .pin8(WR), .pin9(RD), .pin10(1'b0), .pin11(_74541_6_pin11), .pin12(_74541_6_pin12),
    .pin13(_74541_6_pin18[5]), .pin14(_74541_6_pin18[4]), .pin15(_74541_6_pin18[3]),
    .pin16(_74541_6_pin18[2]), .pin17(_74541_6_pin18[1]), .pin18(_74541_6_pin18[0]), .pin19(1'b0),
    .pin20(1'b1));
  RAMSinglePortSel #(.AddrBits(15), .Bits(8)) ramsingleportsel_1 (
    .A({INDEX_RAM_PAGE, _74541_2_pin13, _74541_1_pin11}), .CS(~CE_IR), .WE(~_74541_2_pin12),
    .OE(~_74541_2_pin11), .D({_74541_6_pin2, _74541_5_pin8}));
  RAMSinglePortSel #(.AddrBits(15), .Bits(8)) ramsingleportsel_2 (
    .A({TILE_RAM_PAGE, _74541_6_pin18, _74541_5_pin18}), .CS(~CE_TR), .WE(~_74541_6_pin12),
    .OE(~_74541_6_pin11), .D(ramsingleportsel_2_d));
  BusSplitter #(.Bits(8)) bussplitter_1 (
    .D({_74541_6_pin2, _74541_5_pin8}), .OE(NOT_RD), .D0(bussplitter_1_d0), .D1(bussplitter_1_d1),
    .D2(bussplitter_1_d2), .D3(bussplitter_1_d3), .D4(bussplitter_1_d4), .D5(bussplitter_1_d5),
    .D6(bussplitter_1_d6), .D7(bussplitter_1_d7));
  BusSplitter #(.Bits(8)) bussplitter_2 (
    .D(ramsingleportsel_2_d), .OE(NOT_RD), .D0(bussplitter_2_d0), .D1(bussplitter_2_d1),
    .D2(bussplitter_2_d2), .D3(bussplitter_2_d3), .D4(bussplitter_2_d4), .D5(bussplitter_2_d5),
    .D6(bussplitter_2_d6), .D7(bussplitter_2_d7));
  nor nor_8 (nor_8_out, PIX_CLK, PIX_CLK);
  or or_4 (or_4_out, VBLANK, HBLANK);
  _74245 _74245_1 (
    .pin1(NOT_RD), .pin2(bussplitter_1_d0), .pin3(bussplitter_1_d1), .pin4(bussplitter_1_d2),
    .pin5(bussplitter_1_d3), .pin6(bussplitter_1_d4), .pin7(bussplitter_1_d5), .pin8(bussplitter_1_d6),
    .pin9(bussplitter_1_d7), .pin10(1'b0), .pin11(D[7]), .pin12(D[6]), .pin13(D[5]), .pin14(D[4]),
    .pin15(D[3]), .pin16(D[2]), .pin17(D[1]), .pin18(D[0]), .pin19(CE_IR_CPU_BUS), .pin20(1'b1));
  _74245 _74245_2 (
    .pin1(NOT_RD), .pin2(bussplitter_2_d0), .pin3(bussplitter_2_d1), .pin4(bussplitter_2_d2),
    .pin5(bussplitter_2_d3), .pin6(bussplitter_2_d4), .pin7(bussplitter_2_d5), .pin8(bussplitter_2_d6),
    .pin9(bussplitter_2_d7), .pin10(1'b0), .pin11(D[7]), .pin12(D[6]), .pin13(D[5]), .pin14(D[4]),
    .pin15(D[3]), .pin16(D[2]), .pin17(D[1]), .pin18(D[0]), .pin19(CE_TR_CPU_BUS), .pin20(1'b1));
  _74ACT374 _74act374_1 (
    .D0(ramsingleportsel_2_d[0]), .D1(ramsingleportsel_2_d[1]), .D2(ramsingleportsel_2_d[2]),
    .D3(ramsingleportsel_2_d[3]), .D4(ramsingleportsel_2_d[4]), .D5(ramsingleportsel_2_d[5]),
    .D6(ramsingleportsel_2_d[6]), .D7(ramsingleportsel_2_d[7]), .Cp(nor_8_out), .nOE(or_4_out), .O0(PIX[0]),
    .O1(PIX[1]), .O2(PIX[2]), .O3(PIX[3]), .O4(PIX[4]), .O5(PIX[5]), .O6(PIX[6]), .O7(PIX[7]));

  // Notes on the sheet:
  //   X Scroll Offset
  //   Y Scroll Offset
  //   X Coordinate
  //   Y Coordinate
  //   Y Coordinate [0..2]
  //   X Coordinate [3..9]
  //   X Coordinate [0..2]
  //   Y Coordinate [3..9]
  //   Index Ram Data
  //   WE
  //   OE
  //   Index Ram Address (GPU)
  //   Index Ram Address (CPU)
  //   Tile Ram Address (GPU)
  //   Tile Ram Address (CPU)
  //   Tile Ram Data
endmodule
