// Digital circuit timing.dig as structural Verilog
module timing (
  input  PIXCLK,
  input  VBI_CLR,
  output [9:0] COL,
  output [9:0] ROW,
  output HSYNC,
  output HBLANK,
  output VSYNC,
  output VBLANK,
  output INT
);

  wire _4bit_2_ovf, _4bit_4_ovf, _4bit_5_ovf, _4bit_ovf, nand_1_out, nand_2_out, nand_3_out, nand_4_out,
       nand_5_out, nand_6_out, nand_7_out, nand_9_out, nand_10_out, nand_11_out, nand_13_out, nand_14_out,
       nand_15_out, nand_18_out, nand_20_out, nor_1_out, nor_2_out, nor_3_out, nor_5_out, nor_6_out,
       nor_7_out, not_6_out, NOT_COL5, NOT_COL6, NOT_COL8, NOT_ROW2, NOT_ROW4, VBLANK_START;
  wire [3:2] _4bit_3_out, _4bit_6_out;

  CounterPreset #(.Bits(4)) _4bit (
    .en(1'b1), .C(PIXCLK), .dir(1'b0), .in(4'b0000), .ld(1'b0), .clr(~nand_1_out), .out(COL[3:0]),
    .ovf(_4bit_ovf));
  CounterPreset #(.Bits(4)) _4bit_2 (
    .en(_4bit_ovf), .C(PIXCLK), .dir(1'b0), .in(4'b0000), .ld(1'b0), .clr(~nand_1_out), .out(COL[7:4]),
    .ovf(_4bit_2_ovf));
  CounterPreset #(.Bits(4)) _4bit_3 (
    .en(_4bit_2_ovf), .C(PIXCLK), .dir(1'b0), .in(4'b0000), .ld(1'b0), .clr(~nand_1_out),
    .out({_4bit_3_out, COL[9:8]}));  // open: ovf
  CounterPreset #(.Bits(4)) _4bit_4 (
    .en(1'b1), .C(nand_1_out), .dir(1'b0), .in(4'b0000), .ld(1'b0), .clr(~nand_4_out), .out(ROW[3:0]),
    .ovf(_4bit_4_ovf));
  CounterPreset #(.Bits(4)) _4bit_5 (
    .en(_4bit_4_ovf), .C(nand_1_out), .dir(1'b0), .in(4'b0000), .ld(1'b0), .clr(~nand_4_out), .out(ROW[7:4]),
    .ovf(_4bit_5_ovf));
  CounterPreset #(.Bits(4)) _4bit_6 (
    .en(_4bit_5_ovf), .C(nand_1_out), .dir(1'b0), .in(4'b0000), .ld(1'b0), .clr(~nand_4_out),
    .out({_4bit_6_out, ROW[9:8]}));  // open: ovf
  nor nor_1 (nor_1_out, VBLANK_START, VBLANK_START);
  nand nand_1 (nand_1_out, COL[0], COL[0], COL[1], COL[2], COL[3], COL[4], COL[8], COL[9]);
  nand nand_2 (nand_2_out, ROW[2], ROW[3]);
  nor nor_2 (nor_2_out, nor_1_out, nor_3_out);
  nor nor_3 (nor_3_out, nor_2_out, VBI_CLR);
  not not_1 (NOT_ROW2, ROW[2]);
  not not_2 (NOT_ROW4, ROW[4]);
  nand nand_3 (nand_3_out, nand_2_out, nand_2_out);
  nor nor_4 (INT, nor_3_out, nor_3_out);
  not not_3 (NOT_COL5, COL[5]);
  not not_4 (NOT_COL6, COL[6]);
  not not_5 (NOT_COL8, COL[8]);
  nand nand_4 (nand_4_out, nand_3_out, ROW[9]);
  nand nand_5 (nand_5_out, COL[4], COL[4], COL[4], NOT_COL5, NOT_COL6, COL[7], NOT_COL8, COL[9]);
  nand nand_6 (nand_6_out, COL[4], COL[4], COL[4], COL[5], COL[6], COL[7], NOT_COL8, COL[9]);
  nand nand_7 (nand_7_out, COL[7], NOT_COL8);
  nand nand_8 (VSYNC, ROW[1], NOT_ROW2, ROW[3], NOT_ROW4, ROW[5], ROW[6], ROW[7], ROW[8]);
  nand nand_9 (nand_9_out, ROW[5], ROW[6]);
  nand nand_10 (nand_10_out, ROW[7], ROW[8]);
  nor nor_5 (nor_5_out, ROW[8], ROW[9]);
  nand nand_11 (nand_11_out, nand_5_out, HSYNC);
  nand nand_12 (HSYNC, nand_11_out, nand_6_out);
  nand nand_13 (nand_13_out, nand_7_out, nand_7_out);
  nand nand_14 (nand_14_out, COL[9], COL[9]);
  nor nor_6 (nor_6_out, nand_9_out, nand_10_out);
  nor nor_7 (nor_7_out, nor_5_out, nor_5_out);
  nand nand_15 (nand_15_out, nand_13_out, COL[9]);
  nand nand_16 (VBLANK_START, nor_6_out, nor_6_out);
  not not_6 (not_6_out, nand_14_out);
  nand nand_17 (HBLANK, nand_15_out, nand_18_out);
  nand nand_18 (nand_18_out, HBLANK, not_6_out);
  nand nand_19 (VBLANK, VBLANK_START, nand_20_out);
  nand nand_20 (nand_20_out, VBLANK, nor_7_out);
endmodule
