// Digital circuit video.dig as structural Verilog
module video (
  input  _25_175_MHz,
  input  [7:0] D,
  input  [21:0] A,
  input  MREQ,
  input  RD,
  input  WR,
  input  IOSELx,
  output [7:0] out_5
);

  wire HSYNC, or_1_out, or_2_out, or_3_out, tile_logic_1_vbi_clr, timing_1_hblank, timing_1_int,
       timing_1_vblank, VSYNC;
  wire [7:0] tile_logic_1_pix;
  wire [9:0] timing_1_col, timing_1_row;

  or or_1 (or_1_out, tile_logic_1_pix[7], tile_logic_1_pix[6], tile_logic_1_pix[5]);
  or or_2 (or_2_out, tile_logic_1_pix[4], tile_logic_1_pix[3], tile_logic_1_pix[2]);
  or or_3 (or_3_out, tile_logic_1_pix[1], tile_logic_1_pix[0]);
  VGA vga_1 (.R(or_1_out), .G(or_2_out), .B(or_3_out), .H(HSYNC), .V(VSYNC), .C(_25_175_MHz));
  timing timing_1 (
    .PIXCLK(_25_175_MHz), .VBI_CLR(tile_logic_1_vbi_clr), .COL(timing_1_col), .ROW(timing_1_row),
    .HSYNC(HSYNC), .HBLANK(timing_1_hblank), .VSYNC(VSYNC), .VBLANK(timing_1_vblank), .INT(timing_1_int));
  LED led_1 (.in(timing_1_int));
  tile_logic tile_logic_1 (
    .COL(timing_1_col), .ROW(timing_1_row), .HBLANK(timing_1_hblank), .VBLANK(timing_1_vblank),
    .PIX_CLK(_25_175_MHz), .D(D), .A(A), .MREQ(MREQ), .RD(RD), .WR(WR), .IOSELx(IOSELx),
    .PIX(tile_logic_1_pix), .VBI_CLR(tile_logic_1_vbi_clr));

  assign out_5 = D;

  // Notes on the sheet:
  //   _25_175_MHz: Hz: 2147483647
  //   MREQ: default 1
  //   RD: default 1
  //   WR: default 1
  //   IOSELx: default 1
endmodule
