// Digital circuit timing.dig as structural Verilog
module timing (
  input  c,
  input  r_int,
  output nvs,
  output nhs,
  output nint,
  output hb,
  output vb,
  output [9:0] col,
  output [9:0] row
);

  wire comparator_1_eq, comparator_2_eq, comparator_3_eq, comparator_4_eq, comparator_5_eq, comparator_6_eq,
       comparator_7_eq, comparator_8_eq, comparator_9_eq;

  CounterPreset #(.maxValue(799), .Bits(10)) Col_Counter (
    .en(1'b1), .C(c), .dir(1'b0), .in({10{1'b0}}), .ld(1'b0), .clr(1'b0), .out(col));  // open: ovf
  CounterPreset #(.maxValue(524), .Bits(10)) Row_Counter (
    .en(1'b1), .C(~comparator_1_eq), .dir(1'b0), .in({10{1'b0}}), .ld(1'b0), .clr(1'b0), .out(row));  // open: ovf
  Comparator #(.Bits(10)) comparator_1 (.a(10'h31f), .b(col), .eq(comparator_1_eq));  // open: gt, lt
  Comparator #(.Bits(10)) comparator_2 (.a(col), .b(10'h290), .eq(comparator_2_eq));  // open: gt, lt
  Comparator #(.Bits(10)) comparator_3 (.a(col), .b(10'h2f0), .eq(comparator_3_eq));  // open: gt, lt
  Comparator #(.Bits(10)) comparator_4 (.a(row), .b(10'h1ea), .eq(comparator_4_eq));  // open: gt, lt
  Comparator #(.Bits(10)) comparator_5 (.a(row), .b(10'h1ec), .eq(comparator_5_eq));  // open: gt, lt
  Comparator #(.Bits(10)) comparator_6 (.a(col), .b(10'h280), .eq(comparator_6_eq));  // open: gt, lt
  Comparator #(.Bits(10)) comparator_7 (.a(col), .b(10'h31f), .eq(comparator_7_eq));  // open: gt, lt
  Comparator #(.Bits(10)) comparator_8 (.a(row), .b(10'h1e0), .eq(comparator_8_eq));  // open: gt, lt
  Comparator #(.Bits(10)) comparator_9 (.a(row), .b({10{1'b0}}), .eq(comparator_9_eq));  // open: gt, lt
  RS_FF_AS rs_ff_as_1 (.S(comparator_8_eq), .R(r_int), .nQ(nint));  // open: Q
  RS_FF_AS rs_ff_as_2 (.S(comparator_2_eq), .R(comparator_3_eq), .nQ(nhs));  // open: Q
  RS_FF_AS rs_ff_as_3 (.S(comparator_4_eq), .R(comparator_5_eq), .nQ(nvs));  // open: Q
  RS_FF_AS rs_ff_as_4 (.S(comparator_6_eq), .R(comparator_7_eq), .Q(hb));  // open: nQ
  RS_FF_AS rs_ff_as_5 (.S(comparator_8_eq), .R(comparator_9_eq), .Q(vb));  // open: nQ
endmodule
